# Fritzing sketch connector_16 (saved by Fritzing 0.9.10b)
circuit board: 4.89373cm x 7.17306cm
breadboards: 1

parts:
  J19 = screw terminal, 8 pins
  J20 = screw terminal, 8 pins
  1-17 = shrouded pin header, 16 pins [form="♂ (shrouded male)"]

nets:
  N1: J19.pin1, 1-17.pin16
  N2: J19.pin2, 1-17.pin15
  N3: J19.pin3, 1-17.pin14
  N4: J19.pin4, 1-17.pin13
  N5: J19.pin5, 1-17.pin12
  N6: J19.pin6, 1-17.pin11
  N7: J19.pin7, 1-17.pin10
  N8: J19.pin8, 1-17.pin9
  N9: J20.pin1, 1-17.pin8
  N10: J20.pin2, 1-17.pin7
  N11: J20.pin3, 1-17.pin6
  N12: J20.pin4, 1-17.pin5
  N13: J20.pin5, 1-17.pin4
  N14: J20.pin6, 1-17.pin3
  N15: J20.pin7, 1-17.pin2
  N16: J20.pin8, 1-17.pin1

notes:
  Ohmpi_connector_16
  8  7  6  5  4  3  2  1
  16 15 14 13 12 11 10 9
