# Fritzing sketch accessoire_ohmpi (saved by Fritzing 0.9.6b)
circuit board: 3.46901cm x 5.3418cm
breadboards: 1

parts:
  J4 = shrouded pin header, 16 pins [form="♂ (shrouded male)"]
  J2 = screw terminal, 8 pins  # not connected
  J3 = screw terminal, 8 pins

nets:
  N1: J4.pin9, J3.pin8
  N2: J4.pin10, J3.pin7
  N3: J4.pin11, J3.pin6
  N4: J4.pin12, J3.pin5
  N5: J4.pin13, J3.pin4
  N6: J4.pin14, J3.pin3
  N7: J4.pin15, J3.pin2
  N8: J4.pin16, J3.pin1
