# Fritzing sketch mux.2023.0.1 (saved by Fritzing 0.9.10b)
circuit board: 28.7141cm x 37.3714cm
breadboards: 1

parts:
  Q1 = MOSFET-NCHANNEL [part_number=ZVN4310A package=to-92]
  OMRON1 = OMRON PCB Power Relay – G5LE [part_number="G5LE-1\r\n" package=THT]
  D1 = Diode [part_number=1N4007 package=diode-1n4001]
  Q2 = MOSFET-NCHANNEL [part_number=ZVN4310A package=to-92]
  OMRON2 = OMRON PCB Power Relay – G5LE [part_number="G5LE-1\r\n" package=THT]
  D2 = Diode [part_number=1N4007 package=diode-1n4001]
  OMRON3 = OMRON PCB Power Relay – G5LE [part_number="G5LE-1\r\n" package=THT]
  D3 = Diode [part_number=1N4007 package=diode-1n4001]
  OMRON5 = OMRON PCB Power Relay – G5LE [part_number="G5LE-1\r\n" package=THT]
  OMRON4 = OMRON PCB Power Relay – G5LE [part_number="G5LE-1\r\n" package=THT]
  D4 = Diode [part_number=1N4007 package=diode-1n4001]
  D5 = Diode [part_number=1N4007 package=diode-1n4001]
  Q4 = MOSFET-NCHANNEL [part_number=ZVN4310A package=to-92]
  OMRON6 = OMRON PCB Power Relay – G5LE [part_number="G5LE-1\r\n" package=THT]
  OMRON7 = OMRON PCB Power Relay – G5LE [part_number="G5LE-1\r\n" package=THT]
  D6 = Diode [part_number=1N4007 package=diode-1n4001]
  D7 = Diode [part_number=1N4007 package=diode-1n4001]
  Q8 = MOSFET-NCHANNEL [part_number=ZVN4310A package=to-92]
  OMRON10 = OMRON PCB Power Relay – G5LE [part_number="G5LE-1\r\n" package=THT]
  OMRON11 = OMRON PCB Power Relay – G5LE [part_number="G5LE-1\r\n" package=THT]
  OMRON9 = OMRON PCB Power Relay – G5LE [part_number="G5LE-1\r\n" package=THT]
  OMRON8 = OMRON PCB Power Relay – G5LE [part_number="G5LE-1\r\n" package=THT]
  D9 = Diode [part_number=1N4007 package=diode-1n4001]
  D11 = Diode [part_number=1N4007 package=diode-1n4001]
  D8 = Diode [part_number=1N4007 package=diode-1n4001]
  D10 = Diode [part_number=1N4007 package=diode-1n4001]
  Q12 = MOSFET-NCHANNEL [part_number=ZVN4310A package=to-92]
  OMRON14 = OMRON PCB Power Relay – G5LE [part_number="G5LE-1\r\n" package=THT]
  OMRON12 = OMRON PCB Power Relay – G5LE [part_number="G5LE-1\r\n" package=THT]
  OMRON13 = OMRON PCB Power Relay – G5LE [part_number="G5LE-1\r\n" package=THT]
  OMRON15 = OMRON PCB Power Relay – G5LE [part_number="G5LE-1\r\n" package=THT]
  D14 = Diode [part_number=1N4007 package=diode-1n4001]
  D15 = Diode [part_number=1N4007 package=diode-1n4001]
  D12 = Diode [part_number=1N4007 package=diode-1n4001]
  D13 = Diode [part_number=1N4007 package=diode-1n4001]
  Q11 = MOSFET-NCHANNEL [part_number=ZVN4310A package=to-92]
  Q3 = MOSFET-NCHANNEL [part_number=ZVN4310A package=to-92]
  Q5 = MOSFET-NCHANNEL [part_number=ZVN4310A package=to-92]
  Q6 = MOSFET-NCHANNEL [part_number=ZVN4310A package=to-92]
  Q7 = MOSFET-NCHANNEL [part_number=ZVN4310A package=to-92]
  Q9 = MOSFET-NCHANNEL [part_number=ZVN4310A package=to-92]
  Q10 = MOSFET-NCHANNEL [part_number=ZVN4310A package=to-92]
  Q13 = MOSFET-NCHANNEL [part_number=ZVN4310A package=to-92]
  Q14 = MOSFET-NCHANNEL [part_number=ZVN4310A package=to-92]
  Q15 = MOSFET-NCHANNEL [part_number=ZVN4310A package=to-92]
  TCA9548 = Adafruit TCA9548A [part_number=TCA9548]
  MCP23017-1 = MCP23017 I2C I/O Expander
  Q16 = MOSFET-NCHANNEL [part_number=ZVN4310A package=to-92]
  OMRON16 = OMRON PCB Power Relay – G5LE [part_number="G5LE-1\r\n" package=THT]
  D16 = Diode [part_number=1N4007 package=diode-1n4001]
  J18 = screw terminal, 2 pins
  J15 = screw terminal, 2 pins
  J17 = screw terminal, 2 pins
  Q31 = MOSFET-NCHANNEL [part_number=ZVN4310A package=to-92]
  Q32 = MOSFET-NCHANNEL [part_number=ZVN4310A package=to-92]
  Q30 = MOSFET-NCHANNEL [part_number=ZVN4310A package=to-92]
  Q29 = MOSFET-NCHANNEL [part_number=ZVN4310A package=to-92]
  Q27 = MOSFET-NCHANNEL [part_number=ZVN4310A package=to-92]
  Q28 = MOSFET-NCHANNEL [part_number=ZVN4310A package=to-92]
  Q24 = MOSFET-NCHANNEL [part_number=ZVN4310A package=to-92]
  Q26 = MOSFET-NCHANNEL [part_number=ZVN4310A package=to-92]
  Q25 = MOSFET-NCHANNEL [part_number=ZVN4310A package=to-92]
  Q23 = MOSFET-NCHANNEL [part_number=ZVN4310A package=to-92]
  Q22 = MOSFET-NCHANNEL [part_number=ZVN4310A package=to-92]
  Q21 = MOSFET-NCHANNEL [part_number=ZVN4310A package=to-92]
  Q20 = MOSFET-NCHANNEL [part_number=ZVN4310A package=to-92]
  Q19 = MOSFET-NCHANNEL [part_number=ZVN4310A package=to-92]
  Q18 = MOSFET-NCHANNEL [part_number=ZVN4310A package=to-92]
  Q17 = MOSFET-NCHANNEL [part_number=ZVN4310A package=to-92]
  OMRON31 = OMRON PCB Power Relay – G5LE [part_number="G5LE-1\r\n" package=THT]
  OMRON32 = OMRON PCB Power Relay – G5LE [part_number="G5LE-1\r\n" package=THT]
  OMRON29 = OMRON PCB Power Relay – G5LE [part_number="G5LE-1\r\n" package=THT]
  OMRON28 = OMRON PCB Power Relay – G5LE [part_number="G5LE-1\r\n" package=THT]
  OMRON30 = OMRON PCB Power Relay – G5LE [part_number="G5LE-1\r\n" package=THT]
  OMRON24 = OMRON PCB Power Relay – G5LE [part_number="G5LE-1\r\n" package=THT]
  OMRON25 = OMRON PCB Power Relay – G5LE [part_number="G5LE-1\r\n" package=THT]
  OMRON27 = OMRON PCB Power Relay – G5LE [part_number="G5LE-1\r\n" package=THT]
  OMRON26 = OMRON PCB Power Relay – G5LE [part_number="G5LE-1\r\n" package=THT]
  OMRON23 = OMRON PCB Power Relay – G5LE [part_number="G5LE-1\r\n" package=THT]
  OMRON22 = OMRON PCB Power Relay – G5LE [part_number="G5LE-1\r\n" package=THT]
  OMRON20 = OMRON PCB Power Relay – G5LE [part_number="G5LE-1\r\n" package=THT]
  OMRON21 = OMRON PCB Power Relay – G5LE [part_number="G5LE-1\r\n" package=THT]
  OMRON18 = OMRON PCB Power Relay – G5LE [part_number="G5LE-1\r\n" package=THT]
  OMRON17 = OMRON PCB Power Relay – G5LE [part_number="G5LE-1\r\n" package=THT]
  D29 = Diode [part_number=1N4007 package=diode-1n4001]
  D28 = Diode [part_number=1N4007 package=diode-1n4001]
  D31 = Diode [part_number=1N4007 package=diode-1n4001]
  D32 = Diode [part_number=1N4007 package=diode-1n4001]
  D30 = Diode [part_number=1N4007 package=diode-1n4001]
  D26 = Diode [part_number=1N4007 package=diode-1n4001]
  D24 = Diode [part_number=1N4007 package=diode-1n4001]
  D27 = Diode [part_number=1N4007 package=diode-1n4001]
  D25 = Diode [part_number=1N4007 package=diode-1n4001]
  D23 = Diode [part_number=1N4007 package=diode-1n4001]
  D22 = Diode [part_number=1N4007 package=diode-1n4001]
  D21 = Diode [part_number=1N4007 package=diode-1n4001]
  D20 = Diode [part_number=1N4007 package=diode-1n4001]
  D19 = Diode [part_number=1N4007 package=diode-1n4001]
  D18 = Diode [part_number=1N4007 package=diode-1n4001]
  D17 = Diode [part_number=1N4007 package=diode-1n4001]
  MCP23017-2 = MCP23017 I2C I/O Expander
  MCP23017-3 = MCP23017 I2C I/O Expander
  Q48 = MOSFET-NCHANNEL [part_number=ZVN4310A package=to-92]
  Q47 = MOSFET-NCHANNEL [part_number=ZVN4310A package=to-92]
  Q46 = MOSFET-NCHANNEL [part_number=ZVN4310A package=to-92]
  Q45 = MOSFET-NCHANNEL [part_number=ZVN4310A package=to-92]
  Q43 = MOSFET-NCHANNEL [part_number=ZVN4310A package=to-92]
  Q44 = MOSFET-NCHANNEL [part_number=ZVN4310A package=to-92]
  Q40 = MOSFET-NCHANNEL [part_number=ZVN4310A package=to-92]
  Q42 = MOSFET-NCHANNEL [part_number=ZVN4310A package=to-92]
  Q41 = MOSFET-NCHANNEL [part_number=ZVN4310A package=to-92]
  Q39 = MOSFET-NCHANNEL [part_number=ZVN4310A package=to-92]
  Q38 = MOSFET-NCHANNEL [part_number=ZVN4310A package=to-92]
  Q37 = MOSFET-NCHANNEL [part_number=ZVN4310A package=to-92]
  Q36 = MOSFET-NCHANNEL [part_number=ZVN4310A package=to-92]
  Q35 = MOSFET-NCHANNEL [part_number=ZVN4310A package=to-92]
  Q34 = MOSFET-NCHANNEL [part_number=ZVN4310A package=to-92]
  Q33 = MOSFET-NCHANNEL [part_number=ZVN4310A package=to-92]
  OMRON48 = OMRON PCB Power Relay – G5LE [part_number="G5LE-1\r\n" package=THT]
  OMRON47 = OMRON PCB Power Relay – G5LE [part_number="G5LE-1\r\n" package=THT]
  OMRON45 = OMRON PCB Power Relay – G5LE [part_number="G5LE-1\r\n" package=THT]
  OMRON44 = OMRON PCB Power Relay – G5LE [part_number="G5LE-1\r\n" package=THT]
  OMRON46 = OMRON PCB Power Relay – G5LE [part_number="G5LE-1\r\n" package=THT]
  OMRON40 = OMRON PCB Power Relay – G5LE [part_number="G5LE-1\r\n" package=THT]
  OMRON41 = OMRON PCB Power Relay – G5LE [part_number="G5LE-1\r\n" package=THT]
  OMRON43 = OMRON PCB Power Relay – G5LE [part_number="G5LE-1\r\n" package=THT]
  OMRON42 = OMRON PCB Power Relay – G5LE [part_number="G5LE-1\r\n" package=THT]
  OMRON39 = OMRON PCB Power Relay – G5LE [part_number="G5LE-1\r\n" package=THT]
  OMRON38 = OMRON PCB Power Relay – G5LE [part_number="G5LE-1\r\n" package=THT]
  OMRON36 = OMRON PCB Power Relay – G5LE [part_number="G5LE-1\r\n" package=THT]
  OMRON37 = OMRON PCB Power Relay – G5LE [part_number="G5LE-1\r\n" package=THT]
  OMRON35 = OMRON PCB Power Relay – G5LE [part_number="G5LE-1\r\n" package=THT]
  OMRON34 = OMRON PCB Power Relay – G5LE [part_number="G5LE-1\r\n" package=THT]
  OMRON33 = OMRON PCB Power Relay – G5LE [part_number="G5LE-1\r\n" package=THT]
  D45 = Diode [part_number=1N4007 package=diode-1n4001]
  D44 = Diode [part_number=1N4007 package=diode-1n4001]
  D48 = Diode [part_number=1N4007 package=diode-1n4001]
  D47 = Diode [part_number=1N4007 package=diode-1n4001]
  D46 = Diode [part_number=1N4007 package=diode-1n4001]
  D42 = Diode [part_number=1N4007 package=diode-1n4001]
  D40 = Diode [part_number=1N4007 package=diode-1n4001]
  D43 = Diode [part_number=1N4007 package=diode-1n4001]
  D41 = Diode [part_number=1N4007 package=diode-1n4001]
  D39 = Diode [part_number=1N4007 package=diode-1n4001]
  D38 = Diode [part_number=1N4007 package=diode-1n4001]
  D37 = Diode [part_number=1N4007 package=diode-1n4001]
  D36 = Diode [part_number=1N4007 package=diode-1n4001]
  D35 = Diode [part_number=1N4007 package=diode-1n4001]
  D34 = Diode [part_number=1N4007 package=diode-1n4001]
  D33 = Diode [part_number=1N4007 package=diode-1n4001]
  MCP23017-4 = MCP23017 I2C I/O Expander
  Q64 = MOSFET-NCHANNEL [part_number=ZVN4310A package=to-92]
  Q63 = MOSFET-NCHANNEL [part_number=ZVN4310A package=to-92]
  Q62 = MOSFET-NCHANNEL [part_number=ZVN4310A package=to-92]
  Q61 = MOSFET-NCHANNEL [part_number=ZVN4310A package=to-92]
  Q59 = MOSFET-NCHANNEL [part_number=ZVN4310A package=to-92]
  Q60 = MOSFET-NCHANNEL [part_number=ZVN4310A package=to-92]
  Q56 = MOSFET-NCHANNEL [part_number=ZVN4310A package=to-92]
  Q58 = MOSFET-NCHANNEL [part_number=ZVN4310A package=to-92]
  Q57 = MOSFET-NCHANNEL [part_number=ZVN4310A package=to-92]
  Q55 = MOSFET-NCHANNEL [part_number=ZVN4310A package=to-92]
  Q54 = MOSFET-NCHANNEL [part_number=ZVN4310A package=to-92]
  Q53 = MOSFET-NCHANNEL [part_number=ZVN4310A package=to-92]
  Q52 = MOSFET-NCHANNEL [part_number=ZVN4310A package=to-92]
  Q51 = MOSFET-NCHANNEL [part_number=ZVN4310A package=to-92]
  Q50 = MOSFET-NCHANNEL [part_number=ZVN4310A package=to-92]
  Q49 = MOSFET-NCHANNEL [part_number=ZVN4310A package=to-92]
  OMRON64 = OMRON PCB Power Relay – G5LE [part_number="G5LE-1\r\n" package=THT]
  OMRON63 = OMRON PCB Power Relay – G5LE [part_number="G5LE-1\r\n" package=THT]
  OMRON61 = OMRON PCB Power Relay – G5LE [part_number="G5LE-1\r\n" package=THT]
  OMRON60 = OMRON PCB Power Relay – G5LE [part_number="G5LE-1\r\n" package=THT]
  OMRON62 = OMRON PCB Power Relay – G5LE [part_number="G5LE-1\r\n" package=THT]
  OMRON56 = OMRON PCB Power Relay – G5LE [part_number="G5LE-1\r\n" package=THT]
  OMRON57 = OMRON PCB Power Relay – G5LE [part_number="G5LE-1\r\n" package=THT]
  OMRON59 = OMRON PCB Power Relay – G5LE [part_number="G5LE-1\r\n" package=THT]
  OMRON58 = OMRON PCB Power Relay – G5LE [part_number="G5LE-1\r\n" package=THT]
  OMRON55 = OMRON PCB Power Relay – G5LE [part_number="G5LE-1\r\n" package=THT]
  OMRON54 = OMRON PCB Power Relay – G5LE [part_number="G5LE-1\r\n" package=THT]
  OMRON52 = OMRON PCB Power Relay – G5LE [part_number="G5LE-1\r\n" package=THT]
  OMRON53 = OMRON PCB Power Relay – G5LE [part_number="G5LE-1\r\n" package=THT]
  OMRON51 = OMRON PCB Power Relay – G5LE [part_number="G5LE-1\r\n" package=THT]
  OMRON50 = OMRON PCB Power Relay – G5LE [part_number="G5LE-1\r\n" package=THT]
  OMRON49 = OMRON PCB Power Relay – G5LE [part_number="G5LE-1\r\n" package=THT]
  D61 = Diode [part_number=1N4007 package=diode-1n4001]
  D60 = Diode [part_number=1N4007 package=diode-1n4001]
  D64 = Diode [part_number=1N4007 package=diode-1n4001]
  D63 = Diode [part_number=1N4007 package=diode-1n4001]
  D62 = Diode [part_number=1N4007 package=diode-1n4001]
  D58 = Diode [part_number=1N4007 package=diode-1n4001]
  D56 = Diode [part_number=1N4007 package=diode-1n4001]
  D59 = Diode [part_number=1N4007 package=diode-1n4001]
  D57 = Diode [part_number=1N4007 package=diode-1n4001]
  D55 = Diode [part_number=1N4007 package=diode-1n4001]
  D54 = Diode [part_number=1N4007 package=diode-1n4001]
  D53 = Diode [part_number=1N4007 package=diode-1n4001]
  D52 = Diode [part_number=1N4007 package=diode-1n4001]
  D51 = Diode [part_number=1N4007 package=diode-1n4001]
  D50 = Diode [part_number=1N4007 package=diode-1n4001]
  D49 = Diode [part_number=1N4007 package=diode-1n4001]
  J19 = male pin header, 3 pins [form="♂ (male)"]
  J20 = male pin header, 3 pins [form="♂ (male)"]
  J21 = male pin header, 3 pins [form="♂ (male)"]
  I2C = shrouded pin header, 6 pins [form="♂ (shrouded male)"]
  1-16 = shrouded pin header, 16 pins [form="♂ (shrouded male)"]
  17-32 = shrouded pin header, 16 pins [form="♂ (shrouded male)"]
  33-48 = shrouded pin header, 16 pins [form="♂ (shrouded male)"]
  49-64 = shrouded pin header, 16 pins [form="♂ (shrouded male)"]
  R1 = Resistor [tolerance=±5% power=0.25 resistance=220 package=THT]
  R3 = Resistor [tolerance=±5% power=0.25 resistance=100k package=THT]
  R2 = Resistor [tolerance=±5% power=0.25 resistance=100k package=THT]
  R4 = Resistor [tolerance=±5% power=0.25 resistance=100k package=THT]
  R5 = Resistor [tolerance=±5% power=0.25 resistance=100k package=THT]
  R6 = Resistor [tolerance=±5% power=0.25 resistance=100k package=THT]
  R7 = Resistor [tolerance=±5% power=0.25 resistance=100k package=THT]
  R8 = Resistor [tolerance=±5% power=0.25 resistance=100k package=THT]
  R9 = Resistor [tolerance=±5% power=0.25 resistance=100k package=THT]
  R10 = Resistor [tolerance=±5% power=0.25 resistance=100k package=THT]
  R11 = Resistor [tolerance=±5% power=0.25 resistance=100k package=THT]
  R12 = Resistor [tolerance=±5% power=0.25 resistance=100k package=THT]
  R13 = Resistor [tolerance=±5% power=0.25 resistance=100k package=THT]
  R14 = Resistor [tolerance=±5% power=0.25 resistance=100k package=THT]
  R15 = Resistor [tolerance=±5% power=0.25 resistance=100k package=THT]
  R16 = Resistor [tolerance=±5% power=0.25 resistance=100k package=THT]
  R32 = Resistor [tolerance=±5% power=0.25 resistance=100k package=THT]
  R30 = Resistor [tolerance=±5% power=0.25 resistance=100k package=THT]
  R29 = Resistor [tolerance=±5% power=0.25 resistance=100k package=THT]
  R31 = Resistor [tolerance=±5% power=0.25 resistance=100k package=THT]
  R28 = Resistor [tolerance=±5% power=0.25 resistance=100k package=THT]
  R27 = Resistor [tolerance=±5% power=0.25 resistance=100k package=THT]
  R26 = Resistor [tolerance=±5% power=0.25 resistance=100k package=THT]
  R25 = Resistor [tolerance=±5% power=0.25 resistance=100k package=THT]
  R24 = Resistor [tolerance=±5% power=0.25 resistance=100k package=THT]
  R23 = Resistor [tolerance=±5% power=0.25 resistance=100k package=THT]
  R21 = Resistor [tolerance=±5% power=0.25 resistance=100k package=THT]
  R20 = Resistor [tolerance=±5% power=0.25 resistance=100k package=THT]
  R19 = Resistor [tolerance=±5% power=0.25 resistance=100k package=THT]
  R18 = Resistor [tolerance=±5% power=0.25 resistance=100k package=THT]
  R17 = Resistor [tolerance=±5% power=0.25 resistance=100k package=THT]
  R33 = Resistor [tolerance=±5% power=0.25 resistance=100k package=THT]
  R34 = Resistor [tolerance=±5% power=0.25 resistance=100k package=THT]
  R35 = Resistor [tolerance=±5% power=0.25 resistance=100k package=THT]
  R36 = Resistor [tolerance=±5% power=0.25 resistance=100k package=THT]
  R37 = Resistor [tolerance=±5% power=0.25 resistance=100k package=THT]
  R38 = Resistor [tolerance=±5% power=0.25 resistance=100k package=THT]
  R39 = Resistor [tolerance=±5% power=0.25 resistance=100k package=THT]
  R40 = Resistor [tolerance=±5% power=0.25 resistance=100k package=THT]
  R41 = Resistor [tolerance=±5% power=0.25 resistance=100k package=THT]
  R42 = Resistor [tolerance=±5% power=0.25 resistance=100k package=THT]
  R43 = Resistor [tolerance=±5% power=0.25 resistance=100k package=THT]
  R44 = Resistor [tolerance=±5% power=0.25 resistance=100k package=THT]
  R45 = Resistor [tolerance=±5% power=0.25 resistance=100k package=THT]
  R46 = Resistor [tolerance=±5% power=0.25 resistance=100k package=THT]
  R47 = Resistor [tolerance=±5% power=0.25 resistance=100k package=THT]
  R48 = Resistor [tolerance=±5% power=0.25 resistance=100k package=THT]
  R64 = Resistor [tolerance=±5% power=0.25 resistance=100k package=THT]
  R63 = Resistor [tolerance=±5% power=0.25 resistance=100k package=THT]
  R62 = Resistor [tolerance=±5% power=0.25 resistance=100k package=THT]
  R61 = Resistor [tolerance=±5% power=0.25 resistance=100k package=THT]
  R60 = Resistor [tolerance=±5% power=0.25 resistance=100k package=THT]
  R59 = Resistor [tolerance=±5% power=0.25 resistance=100k package=THT]
  R58 = Resistor [tolerance=±5% power=0.25 resistance=100k package=THT]
  R57 = Resistor [tolerance=±5% power=0.25 resistance=100k package=THT]
  R56 = Resistor [tolerance=±5% power=0.25 resistance=100k package=THT]
  R55 = Resistor [tolerance=±5% power=0.25 resistance=100k package=THT]
  R54 = Resistor [tolerance=±5% power=0.25 resistance=100k package=THT]
  R53 = Resistor [tolerance=±5% power=0.25 resistance=100k package=THT]
  R52 = Resistor [tolerance=±5% power=0.25 resistance=100k package=THT]
  R51 = Resistor [tolerance=±5% power=0.25 resistance=100k package=THT]
  R50 = Resistor [tolerance=±5% power=0.25 resistance=100k package=THT]
  R49 = Resistor [tolerance=±5% power=0.25 resistance=100k package=THT]
  R22 = Resistor [tolerance=±5% power=0.25 resistance=100k package=THT]
  OMRON19 = OMRON PCB Power Relay – G5LE [part_number="G5LE-1\r\n" package=THT]
  R65 = Resistor [tolerance=±5% power=0.25 resistance=4.7k package=THT]
  R66 = Resistor [tolerance=±5% power=0.25 resistance=4.7k package=THT]
  R67 = Resistor [tolerance=±5% power=0.25 resistance=4.7k package=THT]
  R68 = Resistor [tolerance=±5% power=0.25 resistance=4.7k package=THT]
  R69 = Resistor [tolerance=±5% power=0.25 resistance=4.7k package=THT]
  R70 = Resistor [tolerance=±5% power=0.25 resistance=4.7k package=THT]
  R71 = Resistor [tolerance=±5% power=0.25 resistance=4.7k package=THT]
  R72 = Resistor [tolerance=±5% power=0.25 resistance=4.7k package=THT]
  C1 = Ceramic Capacitor [capacitance=100nF voltage=35V package="100 mil [THT, multilayer]"]
  C3 = Ceramic Capacitor [capacitance=100nF voltage=35V package="100 mil [THT, multilayer]"]
  C2 = Ceramic Capacitor [capacitance=100nF voltage=35V package="100 mil [THT, multilayer]"]
  C4 = Ceramic Capacitor [capacitance=100nF voltage=35V package="100 mil [THT, multilayer]"]

nets:
  GND: Q1.S, Q2.S, Q4.S, Q8.S, Q12.S, Q11.S, Q3.S, Q5.S, Q6.S, Q7.S, Q9.S, Q10.S, Q13.S, Q14.S, Q15.S, TCA9548.GND, MCP23017-1.VSS, MCP23017-1.A0, MCP23017-1.A1, MCP23017-1.A2, Q16.S, J18.pin2, J15.pin2, Q31.S, Q32.S, Q30.S, Q29.S, Q27.S, Q28.S, Q24.S, Q26.S, Q25.S, Q23.S, Q22.S, Q21.S, Q20.S, Q19.S, Q18.S, Q17.S, MCP23017-2.VSS, MCP23017-2.A0, MCP23017-2.A1, MCP23017-2.A2, MCP23017-3.VSS, MCP23017-3.A0, MCP23017-3.A1, MCP23017-3.A2, Q48.S, Q47.S, Q46.S, Q45.S, Q43.S, Q44.S, Q40.S, Q42.S, Q41.S, Q39.S, Q38.S, Q37.S, Q36.S, Q35.S, Q34.S, Q33.S, MCP23017-4.VSS, MCP23017-4.A0, MCP23017-4.A1, MCP23017-4.A2, Q64.S, Q63.S, Q62.S, Q61.S, Q59.S, Q60.S, Q56.S, Q58.S, Q57.S, Q55.S, Q54.S, Q53.S, Q52.S, Q51.S, Q50.S, Q49.S, J19.pin3, J20.pin3, J21.pin3, I2C.pin3, R1.Pin_1, R3.Pin_1, R2.Pin_1, R4.Pin_1, R5.Pin_1, R6.Pin_1, R7.Pin_1, R8.Pin_1, R9.Pin_1, R10.Pin_1, R11.Pin_1, R12.Pin_1, R13.Pin_1, R14.Pin_1, R15.Pin_1, R16.Pin_0, R32.Pin_1, R30.Pin_0, R29.Pin_0, R31.Pin_1, R28.Pin_0, R27.Pin_0, R26.Pin_0, R25.Pin_0, R24.Pin_0, R23.Pin_0, R21.Pin_0, R20.Pin_0, R19.Pin_0, R18.Pin_0, R17.Pin_0, R33.Pin_0, R34.Pin_0, R35.Pin_0, R36.Pin_0, R37.Pin_0, R38.Pin_0, R39.Pin_0, R40.Pin_0, R41.Pin_0, R42.Pin_0, R43.Pin_0, R44.Pin_0, R45.Pin_0, R46.Pin_0, R47.Pin_0, R48.Pin_0, R64.Pin_0, R63.Pin_0, R62.Pin_0, R61.Pin_0, R60.Pin_0, R59.Pin_0, R58.Pin_0, R57.Pin_0, R56.Pin_0, R55.Pin_0, R54.Pin_0, R53.Pin_0, R52.Pin_0, R51.Pin_0, R50.Pin_0, R49.Pin_0, R22.Pin_0, C1.0, C3.0, C2.0, C4.0
  N1: Q1.G, MCP23017-1.GPA0, R1.Pin_0
  N2: Q1.D, OMRON1.COIL1, D1.A
  N3: OMRON1.A, 1-16.pin16
  N4: OMRON1.C, OMRON2.C, OMRON3.C, OMRON5.C, OMRON4.C, OMRON6.C, OMRON7.C, OMRON10.C, OMRON11.C, OMRON9.C, OMRON8.C, OMRON14.C, OMRON12.C, OMRON13.C, OMRON15.C, OMRON16.C, J17.pin1, OMRON31.C, OMRON32.C, OMRON29.C, OMRON28.C, OMRON30.C, OMRON24.C, OMRON25.C, OMRON27.C, OMRON26.C, OMRON23.C, OMRON22.C, OMRON20.C, OMRON21.C, OMRON18.C, OMRON17.C, OMRON48.C, OMRON47.C, OMRON45.C, OMRON44.C, OMRON46.C, OMRON40.C, OMRON41.C, OMRON43.C, OMRON42.C, OMRON39.C, OMRON38.C, OMRON36.C, OMRON37.C, OMRON35.C, OMRON34.C, OMRON33.C, OMRON64.C, OMRON63.C, OMRON61.C, OMRON60.C, OMRON62.C, OMRON56.C, OMRON57.C, OMRON59.C, OMRON58.C, OMRON55.C, OMRON54.C, OMRON52.C, OMRON53.C, OMRON51.C, OMRON50.C, OMRON49.C, OMRON19.C
  +12V: OMRON1.COIL2, D1.C, OMRON2.COIL2, D2.C, OMRON3.COIL2, D3.C, OMRON5.COIL2, OMRON4.COIL2, D4.C, D5.C, OMRON6.COIL2, OMRON7.COIL2, D6.C, D7.C, OMRON10.COIL2, OMRON11.COIL2, OMRON9.COIL2, OMRON8.COIL2, D9.C, D11.C, D8.C, D10.C, OMRON14.COIL2, OMRON12.COIL2, OMRON13.COIL2, OMRON15.COIL2, D14.C, D15.C, D12.C, D13.C, OMRON16.COIL2, D16.C, J18.pin1, J15.pin1, OMRON31.COIL2, OMRON32.COIL2, OMRON29.COIL2, OMRON28.COIL2, OMRON30.COIL2, OMRON24.COIL2, OMRON25.COIL2, OMRON27.COIL2, OMRON26.COIL2, OMRON23.COIL2, OMRON22.COIL2, OMRON20.COIL2, OMRON21.COIL2, OMRON18.COIL2, OMRON17.COIL2, D29.C, D28.C, D31.C, D32.C, D30.C, D26.C, D24.C, D27.C, D25.C, D23.C, D22.C, D21.C, D20.C, D19.C, D18.C, D17.C, OMRON48.COIL2, OMRON47.COIL2, OMRON45.COIL2, OMRON44.COIL2, OMRON46.COIL2, OMRON40.COIL2, OMRON41.COIL2, OMRON43.COIL2, OMRON42.COIL2, OMRON39.COIL2, OMRON38.COIL2, OMRON36.COIL2, OMRON37.COIL2, OMRON35.COIL2, OMRON34.COIL2, OMRON33.COIL2, D45.C, D44.C, D48.C, D47.C, D46.C, D42.C, D40.C, D43.C, D41.C, D39.C, D38.C, D37.C, D36.C, D35.C, D34.C, D33.C, OMRON64.COIL2, OMRON63.COIL2, OMRON61.COIL2, OMRON60.COIL2, OMRON62.COIL2, OMRON56.COIL2, OMRON57.COIL2, OMRON59.COIL2, OMRON58.COIL2, OMRON55.COIL2, OMRON54.COIL2, OMRON52.COIL2, OMRON53.COIL2, OMRON51.COIL2, OMRON50.COIL2, OMRON49.COIL2, D61.C, D60.C, D64.C, D63.C, D62.C, D58.C, D56.C, D59.C, D57.C, D55.C, D54.C, D53.C, D52.C, D51.C, D50.C, D49.C, OMRON19.COIL2
  N5: Q2.G, MCP23017-1.GPA1, R2.Pin_0
  N6: Q2.D, OMRON2.COIL1, D2.A
  N7: OMRON2.A, 1-16.pin15
  N8: OMRON3.A, 1-16.pin14
  N9: OMRON3.COIL1, D3.A, Q3.D
  N10: OMRON5.A, 1-16.pin12
  N11: OMRON5.COIL1, D5.A, Q5.D
  N12: OMRON4.A, 1-16.pin13
  N13: OMRON4.COIL1, D4.A, Q4.D
  N14: Q4.G, MCP23017-1.GPA3, R4.Pin_0
  N15: OMRON6.A, 1-16.pin11
  N16: OMRON6.COIL1, D6.A, Q6.D
  N17: OMRON7.A, 1-16.pin10
  N18: OMRON7.COIL1, D7.A, Q7.D
  N19: Q8.G, MCP23017-1.GPA7, R8.Pin_0
  N20: Q8.D, OMRON8.COIL1, D8.A
  N21: OMRON10.A, 1-16.pin7
  N22: OMRON10.COIL1, D10.A, Q10.D
  N23: OMRON11.A, 1-16.pin6
  N24: OMRON11.COIL1, D11.A, Q11.D
  N25: OMRON9.A, 1-16.pin8
  N26: OMRON9.COIL1, D9.A, Q9.D
  N27: OMRON8.A, 1-16.pin9
  N28: Q12.G, MCP23017-1.GPB3, R12.Pin_0
  N29: Q12.D, OMRON12.COIL1, D12.A
  N30: OMRON14.A, 1-16.pin3
  N31: OMRON14.COIL1, D14.A, Q14.D
  N32: OMRON12.A, 1-16.pin5
  N33: OMRON13.A, 1-16.pin4
  N34: OMRON13.COIL1, D13.A, Q13.D
  N35: OMRON15.A, 1-16.pin2
  N36: OMRON15.COIL1, D15.A, Q15.D
  N37: Q11.G, MCP23017-1.GPB2, R11.Pin_0
  N38: Q3.G, MCP23017-1.GPA2, R3.Pin_0
  N39: Q5.G, MCP23017-1.GPA4, R5.Pin_0
  N40: Q6.G, MCP23017-1.GPA5, R6.Pin_0
  N41: Q7.G, MCP23017-1.GPA6, R7.Pin_0
  N42: Q9.G, MCP23017-1.GPB0, R9.Pin_0
  N43: Q10.G, MCP23017-1.GPB1, R10.Pin_0
  N44: Q13.G, MCP23017-1.GPB4, R13.Pin_0
  N45: Q14.G, MCP23017-1.GPB5, R14.Pin_0
  N46: Q15.G, MCP23017-1.GPB6, R15.Pin_0
  N47: TCA9548.4SDA, MCP23017-4.SDA, R72.Pin_0
  N48: TCA9548.4SCL, MCP23017-4.SCL, R71.Pin_1
  N49: TCA9548.5SDA, MCP23017-3.SDA, R66.Pin_0
  N50: TCA9548.5SCL, MCP23017-3.SCL, R65.Pin_1
  N51: TCA9548.6SDA, MCP23017-2.SDA, R67.Pin_0
  N52: TCA9548.6SCL, MCP23017-2.SCL, R68.Pin_1
  N53: TCA9548.7SDA, MCP23017-1.SDA, R70.Pin_0
  N54: TCA9548.7SCL, MCP23017-1.SCL, R69.Pin_1
  5V: TCA9548.VCC, MCP23017-1.VDD, MCP23017-1.RESET, MCP23017-2.VDD, MCP23017-2.RESET, MCP23017-3.VDD, MCP23017-3.RESET, MCP23017-4.VDD, MCP23017-4.RESET, J19.pin1, J20.pin1, J21.pin1, I2C.pin4, R65.Pin_0, R66.Pin_1, R67.Pin_1, R68.Pin_0, R69.Pin_0, R70.Pin_1, R71.Pin_0, R72.Pin_1, C1.1, C3.1, C2.1, C4.1
  N55: TCA9548.INPUTSDA, I2C.pin2
  N56: TCA9548.INPUTSCL, I2C.pin1
  N57: TCA9548.A0, J21.pin2
  N58: TCA9548.A1, J20.pin2
  N59: TCA9548.A2, J19.pin2
  N60: MCP23017-1.GPB7, Q16.G, R16.Pin_1
  N61: Q16.D, OMRON16.COIL1, D16.A
  N62: OMRON16.A, 1-16.pin1
  N63: Q31.G, MCP23017-2.GPB6, R31.Pin_0
  N64: Q31.D, OMRON31.COIL1, D31.A
  N65: Q32.G, MCP23017-2.GPB7, R32.Pin_0
  N66: Q32.D, OMRON32.COIL1, D32.A
  N67: Q30.G, MCP23017-2.GPB5, R30.Pin_1
  N68: Q30.D, OMRON30.COIL1, D30.A
  N69: Q29.G, MCP23017-2.GPB4, R29.Pin_1
  N70: Q29.D, OMRON29.COIL1, D29.A
  N71: Q27.G, MCP23017-2.GPB2, R27.Pin_1
  N72: Q27.D, OMRON27.COIL1, D27.A
  N73: Q28.G, MCP23017-2.GPB3, R28.Pin_1
  N74: Q28.D, OMRON28.COIL1, D28.A
  N75: Q24.G, MCP23017-2.GPA7, R24.Pin_1
  N76: Q24.D, OMRON24.COIL1, D24.A
  N77: Q26.G, MCP23017-2.GPB1, R26.Pin_1
  N78: Q26.D, OMRON26.COIL1, D26.A
  N79: Q25.G, MCP23017-2.GPB0, R25.Pin_1
  N80: Q25.D, OMRON25.COIL1, D25.A
  N81: Q23.G, MCP23017-2.GPA6, R23.Pin_1
  N82: Q23.D, OMRON23.COIL1, D23.A
  N83: Q22.G, MCP23017-2.GPA5, R22.Pin_1
  N84: Q22.D, OMRON22.COIL1, D22.A
  N85: Q21.G, MCP23017-2.GPA4, R21.Pin_1
  N86: Q21.D, OMRON21.COIL1, D21.A
  N87: Q20.G, MCP23017-2.GPA3, R20.Pin_1
  N88: Q20.D, OMRON20.COIL1, D20.A
  N89: Q19.G, MCP23017-2.GPA2, R19.Pin_1
  N90: Q19.D, D19.A, OMRON19.COIL1
  N91: Q18.G, MCP23017-2.GPA1, R18.Pin_1
  N92: Q18.D, OMRON18.COIL1, D18.A
  N93: Q17.G, MCP23017-2.GPA0, R17.Pin_1
  N94: Q17.D, OMRON17.COIL1, D17.A
  N95: OMRON31.A, 17-32.pin2
  N96: OMRON32.A, 17-32.pin1
  N97: OMRON29.A, 17-32.pin4
  N98: OMRON28.A, 17-32.pin5
  N99: OMRON30.A, 17-32.pin3
  N100: OMRON24.A, 17-32.pin9
  N101: OMRON25.A, 17-32.pin8
  N102: OMRON27.A, 17-32.pin6
  N103: OMRON26.A, 17-32.pin7
  N104: OMRON23.A, 17-32.pin10
  N105: OMRON22.A, 17-32.pin11
  N106: OMRON20.A, 17-32.pin13
  N107: OMRON21.A, 17-32.pin12
  N108: OMRON18.A, 17-32.pin15
  N109: OMRON17.A, 17-32.pin16
  N110: MCP23017-3.GPB0, Q41.G, R41.Pin_1
  N111: MCP23017-3.GPB1, Q42.G, R42.Pin_1
  N112: MCP23017-3.GPB2, Q43.G, R43.Pin_1
  N113: MCP23017-3.GPB3, Q44.G, R44.Pin_1
  N114: MCP23017-3.GPB4, Q45.G, R45.Pin_1
  N115: MCP23017-3.GPB5, Q46.G, R46.Pin_1
  N116: MCP23017-3.GPB6, Q47.G, R47.Pin_1
  N117: MCP23017-3.GPB7, Q48.G, R48.Pin_1
  N118: MCP23017-3.GPA0, Q33.G, R33.Pin_1
  N119: MCP23017-3.GPA1, Q34.G, R34.Pin_1
  N120: MCP23017-3.GPA2, Q35.G, R35.Pin_1
  N121: MCP23017-3.GPA3, Q36.G, R36.Pin_1
  N122: MCP23017-3.GPA4, Q37.G, R37.Pin_1
  N123: MCP23017-3.GPA5, Q38.G, R38.Pin_1
  N124: MCP23017-3.GPA6, Q39.G, R39.Pin_1
  N125: MCP23017-3.GPA7, Q40.G, R40.Pin_1
  N126: Q48.D, OMRON48.COIL1, D48.A
  N127: Q47.D, OMRON47.COIL1, D47.A
  N128: Q46.D, OMRON46.COIL1, D46.A
  N129: Q45.D, OMRON45.COIL1, D45.A
  N130: Q43.D, OMRON43.COIL1, D43.A
  N131: Q44.D, OMRON44.COIL1, D44.A
  N132: Q40.D, OMRON40.COIL1, D40.A
  N133: Q42.D, OMRON42.COIL1, D42.A
  N134: Q41.D, OMRON41.COIL1, D41.A
  N135: Q39.D, OMRON39.COIL1, D39.A
  N136: Q38.D, OMRON38.COIL1, D38.A
  N137: Q37.D, OMRON37.COIL1, D37.A
  N138: Q36.D, OMRON36.COIL1, D36.A
  N139: Q35.D, OMRON35.COIL1, D35.A
  N140: Q34.D, OMRON34.COIL1, D34.A
  N141: Q33.D, OMRON33.COIL1, D33.A
  N142: OMRON48.A, 33-48.pin1
  N143: OMRON47.A, 33-48.pin2
  N144: OMRON45.A, 33-48.pin4
  N145: OMRON44.A, 33-48.pin5
  N146: OMRON46.A, 33-48.pin3
  N147: OMRON40.A, 33-48.pin9
  N148: OMRON41.A, 33-48.pin8
  N149: OMRON43.A, 33-48.pin6
  N150: OMRON42.A, 33-48.pin7
  N151: OMRON39.A, 33-48.pin10
  N152: OMRON38.A, 33-48.pin11
  N153: OMRON36.A, 33-48.pin13
  N154: OMRON37.A, 33-48.pin12
  N155: OMRON35.A, 33-48.pin14
  N156: OMRON34.A, 33-48.pin15
  N157: OMRON33.A, 33-48.pin16
  N158: MCP23017-4.GPB0, Q57.G, R57.Pin_1
  N159: MCP23017-4.GPB1, Q58.G, R58.Pin_1
  N160: MCP23017-4.GPB2, Q59.G, R59.Pin_1
  N161: MCP23017-4.GPB3, Q60.G, R60.Pin_1
  N162: MCP23017-4.GPB4, Q61.G, R61.Pin_1
  N163: MCP23017-4.GPB5, Q62.G, R62.Pin_1
  N164: MCP23017-4.GPB6, Q63.G, R63.Pin_1
  N165: MCP23017-4.GPB7, Q64.G, R64.Pin_1
  N166: MCP23017-4.GPA0, Q49.G, R49.Pin_1
  N167: MCP23017-4.GPA1, Q50.G, R50.Pin_1
  N168: MCP23017-4.GPA2, Q51.G, R51.Pin_1
  N169: MCP23017-4.GPA3, Q52.G, R52.Pin_1
  N170: MCP23017-4.GPA4, Q53.G, R53.Pin_1
  N171: MCP23017-4.GPA5, Q54.G, R54.Pin_1
  N172: MCP23017-4.GPA6, Q55.G, R55.Pin_1
  N173: MCP23017-4.GPA7, Q56.G, R56.Pin_1
  N174: Q64.D, OMRON64.COIL1, D64.A
  N175: Q63.D, OMRON63.COIL1, D63.A
  N176: Q62.D, OMRON62.COIL1, D62.A
  N177: Q61.D, OMRON61.COIL1, D61.A
  N178: Q59.D, OMRON59.COIL1, D59.A
  N179: Q60.D, OMRON60.COIL1, D60.A
  N180: Q56.D, OMRON56.COIL1, D56.A
  N181: Q58.D, OMRON58.COIL1, D58.A
  N182: Q57.D, OMRON57.COIL1, D57.A
  N183: Q55.D, OMRON55.COIL1, D55.A
  N184: Q54.D, OMRON54.COIL1, D54.A
  N185: Q53.D, OMRON53.COIL1, D53.A
  N186: Q52.D, OMRON52.COIL1, D52.A
  N187: Q51.D, OMRON51.COIL1, D51.A
  N188: Q50.D, OMRON50.COIL1, D50.A
  N189: Q49.D, OMRON49.COIL1, D49.A
  N190: OMRON64.A, 49-64.pin1
  N191: OMRON63.A, 49-64.pin2
  N192: OMRON61.A, 49-64.pin4
  N193: OMRON60.A, 49-64.pin5
  N194: OMRON62.A, 49-64.pin3
  N195: OMRON56.A, 49-64.pin9
  N196: OMRON57.A, 49-64.pin8
  N197: OMRON59.A, 49-64.pin6
  N198: OMRON58.A, 49-64.pin7
  N199: OMRON55.A, 49-64.pin10
  N200: OMRON54.A, 49-64.pin11
  N201: OMRON52.A, 49-64.pin13
  N202: OMRON53.A, 49-64.pin12
  N203: OMRON51.A, 49-64.pin14
  N204: OMRON50.A, 49-64.pin15
  N205: OMRON49.A, 49-64.pin16
  N206: 17-32.pin14, OMRON19.A

notes:
  mux.2023.0.1
  12V
  GND
  https://gitlab.irstea.fr/reversaal/OhmPi
  Address

custom parts:
  MOSFET-NCHANNEL: Generic NMOS footprint
  Adafruit TCA9548A: You just found the perfect I2C sensor, and you want to wire up two or three or more of them to your Arduino when you realize "Uh oh, this chip has a fixed I2C address, and from what I know about I2C, you cannot have two devices with the same address on the same SDA/SCL pins!" Are you out of luck? You would be, if you didn't have this ultra-cool TCA9548A 1-to-8 I2C multiplexer! Finally, a way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
  MCP23017 I2C I/O Expander: The MCP23017 uses two i2c pins (these can be shared with other i2c devices), and in exchange gives you 16 general purpose pins. You can set each of 16 pins to be input, output, input with a pullup or open drain. There's even the ability to get an interrupt via an external pin when any of the inputs change so you don't have to keep polling the chip.
