# Fritzing sketch card_measure_raspberry_v3.03 (saved by Fritzing 0.9.4)
circuit board: 7.74179cm x 8.33978cm
breadboards: 1

parts:
  LM358-3 = LM358 [package=dip08]
  LM358-2 = LM358 [package=dip08]
  LM358-1 = LM358 [package=dip08]
  R3 = Resistor [tolerance=±5% resistance=220 package=THT]
  R4 = Resistor [tolerance=±5% resistance=220 package=THT]
  R1 = Resistor [tolerance=±5% resistance=220 package=THT]
  R5 = Resistor [tolerance=±0.05% resistance=50 part_number=1 package=THT]
  Composant1 = Adafruit ADS1115 16Bit I2C ADC [part_number="Adafruit #1085"]
  R2 = Resistor [tolerance=±5% resistance=220 package=THT]
  R6 = Resistor [tolerance=±5% resistance=220 package=THT]
  R7 = Resistor [tolerance=±5% resistance=220 package=THT]
  LM358-4 = LM358 [package=dip08]
  R8 = Resistor [tolerance=±5% resistance=220 package=THT]
  R9 = Resistor [tolerance=±5% resistance=220 package=THT]
  J6 = screw terminal, 14 pins

nets:
  N1: LM358-3.G$1_OUT, LM358-3.G$1_-IN, R6.Pin_1
  N2: LM358-3.G$1_+IN, J6.pin12
  GND: LM358-3.G$1_V-, LM358-2.G$1_V-, LM358-1.G$1_V-, R3.Pin_0, R1.Pin_0, R7.Pin_0, LM358-4.G$1_V-, R9.Pin_0, J6.pin5, J6.pin8, J6.pin9, J6.pin13
  N3: LM358-3.G$2_+IN, J6.pin11
  N4: LM358-3.G$2_-IN, LM358-3.G$2_OUT, R8.Pin_1
  12V: LM358-3.G$1_V+, LM358-2.G$1_V+, LM358-1.G$1_V+, LM358-4.G$1_V+, J6.pin14
  N5: LM358-2.G$1_OUT, LM358-2.G$1_-IN, Composant1.AIN0
  N6: LM358-2.G$1_+IN, R3.Pin_1, R4.Pin_0
  N7: LM358-2.G$2_+IN, R1.Pin_1, R2.Pin_0
  N8: LM358-2.G$2_-IN, LM358-2.G$2_OUT, Composant1.AIN1
  N9: LM358-1.G$1_OUT, LM358-1.G$1_-IN, R4.Pin_1
  N10: LM358-1.G$1_+IN, R5.Pin_0, J6.pin10
  N11: LM358-1.G$2_+IN, R5.Pin_1, J6.pin7
  N12: LM358-1.G$2_-IN, LM358-1.G$2_OUT, R2.Pin_1
  N13: Composant1.AIN3, LM358-4.G$2_-IN, LM358-4.G$2_OUT
  N14: Composant1.AIN2, LM358-4.G$1_OUT, LM358-4.G$1_-IN
  5V: Composant1.VDD
  N15: R6.Pin_0, R7.Pin_1, LM358-4.G$1_+IN
  N16: LM358-4.G$2_+IN, R8.Pin_0, R9.Pin_1

notes:
  TX+
  A
  +12V
  TX-
  B
  M(A2)
  N(A3)
  GND
  VDD 5V
  SCL
  SDA
  ADDR
  ALERT
  ADS 1115
  ohmpy card 3.01
  A0
  A1
  +12V RX

custom parts:
  Adafruit ADS1115 16Bit I2C ADC: For microcontrollers without an analog-to-digital converter or when you want a higher-precision ADC, the ADS1115 provides 16-bit precision at 860 samples/second over I2C. The chip can be configured as 4 single-ended input channels, or two differential channels. As a nice bonus, it even includes a programmable gain amplifier, up to x16, to help boost up smaller single/differential signals to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
