# Fritzing sketch card_measure_raspberry_v3.04 (saved by Fritzing 0.9.4)
circuit board: 7.74179cm x 8.44288cm
breadboards: 1

parts:
  LM358-3 = LM358 [package=dip08]
  LM358-2 = LM358 [package=dip08]
  LM358-1 = LM358 [package=dip08]
  R3 = Resistor [tolerance=±0.1% resistance=1k package=THT]
  R4 = Resistor [tolerance=±0.1% resistance=1.5k package=THT]
  R1 = Resistor [tolerance=±0.1% resistance=1k package=THT]
  R5 = Resistor [tolerance=±0.1% resistance=50 package=THT]
  Composant1 = Adafruit ADS1115 16Bit I2C ADC [part_number="Adafruit #1115"]
  R2 = Resistor [tolerance=±0.1% resistance=1.5k package=THT]
  R6 = Resistor [tolerance=±0.1% resistance=1.5k package=THT]
  R7 = Resistor [tolerance=±0.1% resistance=1k package=THT]
  LM358-4 = LM358 [package=dip08]
  R8 = Resistor [tolerance=±0.1% resistance=1.5k package=THT]
  R9 = Resistor [tolerance=±0.1% resistance=1k package=THT]
  J6 = screw terminal, 14 pins
  R11 = Resistor [tolerance=±5% resistance=10M package=THT]
  R13 = Resistor [tolerance=±5% resistance=10M package=THT]
  C1 = Ceramic Capacitor [capacitance=100nF voltage=50V package="100 mil [THT, multilayer]"]
  C2 = Ceramic Capacitor [capacitance=100nF voltage=50V package="100 mil [THT, multilayer]"]
  C4 = Ceramic Capacitor [capacitance=100nF voltage=50V package="100 mil [THT, multilayer]"]
  TRN3-1215 = TRN3-1211
  TRN3-1215_2 = TRN3-1211
  R12 = Resistor [tolerance=±5% resistance=10M package=THT]
  R10 = Resistor [tolerance=±5% resistance=10M package=THT]
  C3 = Ceramic Capacitor [capacitance=100nF voltage=50V package="100 mil [THT, multilayer]"]
  Fuse1 = Fuse

nets:
  N1: LM358-3.G$1_OUT, LM358-3.G$1_-IN, R6.Pin_1
  N2: LM358-3.G$1_+IN, J6.pin12, R12.Pin_1
  GND: LM358-3.G$1_V-, LM358-2.G$1_V-, LM358-1.G$1_V-, R3.Pin_0, R1.Pin_0, Composant1.GND, R7.Pin_0, LM358-4.G$1_V-, R9.Pin_0, J6.pin5, J6.pin8, J6.pin9, J6.pin13, R11.Pin_1, R13.Pin_1, C1.0, C2.0, C4.0, TRN3-1215.pin1, TRN3-1215.pin5, TRN3-1215_2.pin1, TRN3-1215_2.pin5, R12.Pin_0, R10.Pin_0, C3.1
  N3: LM358-3.G$2_+IN, J6.pin11, R13.Pin_0
  N4: LM358-3.G$2_-IN, LM358-3.G$2_OUT, R8.Pin_1
  N5: LM358-3.G$1_V+, LM358-2.G$1_V+, LM358-1.G$1_V+, LM358-4.G$1_V+, C1.1, C2.1, C4.1, TRN3-1215.pin3, TRN3-1215_2.pin3, C3.0
  N6: LM358-2.G$1_OUT, LM358-2.G$1_-IN, Composant1.AIN1
  N7: LM358-2.G$1_+IN, R3.Pin_1, R4.Pin_0
  N8: LM358-2.G$2_+IN, R1.Pin_1, R2.Pin_0
  N9: LM358-2.G$2_-IN, LM358-2.G$2_OUT, Composant1.AIN0
  N10: LM358-1.G$1_OUT, LM358-1.G$1_-IN, R4.Pin_1
  N11: LM358-1.G$1_+IN, R5.Pin_0, R10.Pin_1, Fuse1.Connector1
  N12: LM358-1.G$2_+IN, R5.Pin_1, J6.pin7, R11.Pin_0
  N13: LM358-1.G$2_-IN, LM358-1.G$2_OUT, R2.Pin_1
  N14: Composant1.AIN3, LM358-4.G$1_OUT, LM358-4.G$1_-IN
  N15: Composant1.AIN2, LM358-4.G$2_-IN, LM358-4.G$2_OUT
  N16: Composant1.ALERT, J6.pin4
  N17: Composant1.ADDR, J6.pin3
  N18: Composant1.SDA, J6.pin2
  N19: Composant1.SCL, J6.pin1
  5V: Composant1.VDD, J6.pin6
  N20: R6.Pin_0, R7.Pin_1, LM358-4.G$1_+IN
  N21: LM358-4.G$2_+IN, R8.Pin_0, R9.Pin_1
  N22: J6.pin10, Fuse1.Connector2
  12V: J6.pin14, TRN3-1215.pin2, TRN3-1215_2.pin2

notes:
  TX+
  A
  +12V
  TX-
  B
  M(A2)
  N(A3)
  GND
  VDD 5V
  SCL
  SDA
  ADDR
  ALERT
  ADS 1115
  Ohmpi card 3.03
  A0
  A1
  +12V RX
  GND RX
  N
  M
  Tx-
  Tx+
  Vcc 5
  Alert
  SLC
  https://gitlab.irstea.fr/reversaal/OhmPi

custom parts:
  Adafruit ADS1115 16Bit I2C ADC: For microcontrollers without an analog-to-digital converter or when you want a higher-precision ADC, the ADS1115 provides 16-bit precision at 860 samples/second over I2C. The chip can be configured as 4 single-ended input channels, or two differential channels. As a nice bonus, it even includes a programmable gain amplifier, up to x16, to help boost up smaller single/differential signals to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
  TRN3-1211: DC/DCconverter traco power
  Fuse: Device used to protect against excessive current.
