# Fritzing sketch card_measure_raspberry_v3.08 (saved by Fritzing 0.9.4)
circuit board: 13.4378cm x 8.02292cm
breadboards: 1

parts:
  LM358-3 = LM358 [package=dip08]
  LM358-2 = LM358 [package=dip08]
  LM358-1 = LM358 [package=dip08]
  R3 = Resistor [tolerance=±1% resistance=1k package=THT]
  R4 = Resistor [tolerance=±1% resistance=1.5k package=THT]
  R1 = Resistor [tolerance=±1% resistance=1k package=THT]
  R5 = Resistor [tolerance=±0.05% resistance=50 part_number=1 package=THT]
  Composant1 = Adafruit ADS1115 16Bit I2C ADC [part_number="Adafruit #1085"]
  R2 = Resistor [tolerance=±1% resistance=1.5k package=THT]
  R7 = Resistor [tolerance=±1% resistance=1k package=THT]
  LM358-4 = LM358 [package=dip08]
  R8 = Resistor [tolerance=±1% resistance=1.5k package=THT]
  R9 = Resistor [tolerance=±1% resistance=1k package=THT]
  D2 = Diode [part_number=1N4007 package=diode-1n4001]
  Q3 = MOSFET-NCHANNEL [part_number=ZVN4310A package=to-92]
  OMRON2 = OMRON PCB Power Relay – G5LE [part_number="G5LE-1\r\n" package=THT]
  D4 = Diode [part_number=1N4007 package=diode-1n4001]
  Q5 = MOSFET-NCHANNEL [part_number=ZVN4310A package=to-92]
  OMRON3 = OMRON PCB Power Relay – G5LE [part_number="G5LE-1\r\n" package=THT]
  D5 = Diode [part_number=1N4007 package=diode-1n4001]
  DS1 = DS18B20 1-Wire Temperature Sensor [part_number=DS18B20]
  J7 = double row female pin header, 40 pins [form="♀ (female)"]
  R10 = Resistor [tolerance=±5% resistance=4.7k package=THT]
  R6 = Resistor [tolerance=±1% resistance=1.5k package=THT]
  I2C-MUX = shrouded pin header, 6 pins [form="♂ (shrouded male)"]
  R11 = Resistor [tolerance=±5% resistance=10M package=THT]
  R12 = Resistor [tolerance=±20% resistance=10M package=THT]
  R13 = Resistor [tolerance=±5% resistance=10M package=THT]
  R14 = Resistor [tolerance=±5% resistance=10M package=THT]
  C1 = Ceramic Capacitor [capacitance=100nF voltage=50V package="100 mil [THT, multilayer]"]
  C2 = Ceramic Capacitor [capacitance=100nF voltage=50V package="100 mil [THT, multilayer]"]
  J6 = screw terminal, 8 pins
  C3 = Ceramic Capacitor [capacitance=100nF voltage=50V package="100 mil [THT, multilayer]"]
  C4 = Ceramic Capacitor [capacitance=100nF voltage=50V package="100 mil [THT, multilayer]"]
  THD_15-1211N1 = THD 15-1211N [package="DIP24 [THT]"]
  J8 = Screw terminal - 2 pins [package=THT]
  TRN3-1215 = TRN3-1211
  TRN3-1215_2 = TRN3-1211
  OMRON1 = OMRON PCB Power Relay – G5LE [part_number="G5LE-1\r\n" package=THT]

nets:
  N1: LM358-3.G$1_OUT, LM358-3.G$1_-IN, R6.Pin_1
  N2: LM358-3.G$1_+IN, R11.Pin_1, J6.pin6
  GND: LM358-3.G$1_V-, LM358-2.G$1_V-, LM358-1.G$1_V-, R3.Pin_0, R1.Pin_0, Composant1.GND, R7.Pin_0, LM358-4.G$1_V-, R9.Pin_0, Q3.S, Q5.S, OMRON3.C, DS1.GND, J7.pin40, I2C-MUX.pin3, R11.Pin_0, R12.Pin_1, R13.Pin_1, R14.Pin_1, C1.0, C2.0, J6.pin2, J6.pin7, C3.0, C4.0, THD_15-1211N1.pin_3, TRN3-1215.pin1, TRN3-1215.pin5, TRN3-1215_2.pin1, TRN3-1215_2.pin5
  N3: LM358-3.G$2_+IN, R12.Pin_0, J6.pin5
  N4: LM358-3.G$2_-IN, LM358-3.G$2_OUT, R8.Pin_1
  N5: LM358-3.G$1_V+, LM358-4.G$1_V+, C1.1, C2.1, TRN3-1215.pin3
  N6: LM358-2.G$1_OUT, LM358-2.G$1_-IN, Composant1.AIN1
  N7: LM358-2.G$1_+IN, R3.Pin_1, R4.Pin_0
  N8: LM358-2.G$2_+IN, R1.Pin_1, R2.Pin_0
  N9: LM358-2.G$2_-IN, LM358-2.G$2_OUT, Composant1.AIN0
  N10: LM358-2.G$1_V+, LM358-1.G$1_V+, C3.1, C4.1, TRN3-1215_2.pin3
  N11: LM358-1.G$1_OUT, LM358-1.G$1_-IN, R4.Pin_1
  N12: LM358-1.G$1_+IN, R5.Pin_0, OMRON2.C, R13.Pin_0
  N13: LM358-1.G$2_+IN, R5.Pin_1, R14.Pin_0, OMRON1.A
  N14: LM358-1.G$2_-IN, LM358-1.G$2_OUT, R2.Pin_1
  N15: Composant1.AIN3, LM358-4.G$1_OUT, LM358-4.G$1_-IN
  N16: Composant1.AIN2, LM358-4.G$2_-IN, LM358-4.G$2_OUT
  N17: Composant1.SDA, J7.pin22, I2C-MUX.pin2
  N18: Composant1.SCL, J7.pin23, I2C-MUX.pin1
  N19: Composant1.VDD, J7.pin20, I2C-MUX.pin4
  N20: R7.Pin_1, LM358-4.G$1_+IN, R6.Pin_0
  N21: LM358-4.G$2_+IN, R8.Pin_0, R9.Pin_1
  N22: D2.A, Q3.D, OMRON1.COIL1
  N23: D2.C, OMRON2.COIL2, D4.C, OMRON3.COIL2, D5.C, J6.pin8, THD_15-1211N1.pin_22, TRN3-1215.pin2, TRN3-1215_2.pin2, OMRON1.COIL2
  N24: Q3.G, J7.pin9
  N25: OMRON2.A, OMRON3.B, J6.pin3
  N26: OMRON2.COIL1, D4.A, Q5.D, OMRON3.COIL1, D5.A
  N27: OMRON2.B, OMRON3.A, J6.pin4
  N28: Q5.G, J7.pin8
  N29: DS1.DQ, J7.pin24, R10.Pin_1
  N30: DS1.VDD, J7.pin21, R10.Pin_0
  N31: J6.pin1, OMRON1.C
  N32: THD_15-1211N1.pin_14, J8.pin1
  N33: THD_15-1211N1.pin_16, J8.pin2

notes:
  TX+
  A
  +12V
  TX-
  B
  M(A2)
  N(A3)
  GND
  ADS 1115
  OhmPi card 3.08
  A0
  A1
  +5V
  USB raspberry>
  https://gitlab.irstea.fr/reversaal/OhmPi

custom parts:
  Adafruit ADS1115 16Bit I2C ADC: For microcontrollers without an analog-to-digital converter or when you want a higher-precision ADC, the ADS1115 provides 16-bit precision at 860 samples/second over I2C. The chip can be configured as 4 single-ended input channels, or two differential channels. As a nice bonus, it even includes a programmable gain amplifier, up to x16, to help boost up smaller single/differential signals to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
  MOSFET-NCHANNEL: Generic NMOS footprint
  THD 15-1211N: DC/DC Converters
  TRN3-1211: DC/DCconverter traco power
