# Fritzing sketch card_measure_raspberry_v3.15 (saved by Fritzing 0.9.6b)
circuit board: 13.6124cm x 6.53974cm
breadboards: 1

parts:
  Raspberry_Pi_1 = Raspberry Pi 3 [part_number=RPI-3-V1.2]
  Shunt = Resistor [tolerance=±0.1% resistance=0.2 power=0.25 package=THT]
  R1 = Resistor [tolerance=±5% resistance=1.5k power=0.25 package=THT]
  U2 = Sharp PC817 [package=THT]
  R2 = Resistor [tolerance=±5% resistance=1.5k power=0.25 package=THT]
  U4 = Sharp PC817 [package=THT]
  MCP23008 = Microchip MCP23008 8-bit I/O expander [part_number=MCP23008 package="DIP (Dual Inline) [THT]"]
  U3 = Sharp PC817 [package=THT]
  U1 = Sharp PC817 [part_number=AQY211EH package=THT]
  ADS1115-2 = Adafruit ADS1115 16Bit I2C ADC [part_number="Adafruit #1085"]
  INA282 = ina 282 [chip_label=INA282]
  C1 = Ceramic Capacitor [capacitance=100nF package="100 mil [THT, multilayer]"]
  LM358-1 = LM358 [package=dip08]
  R28 = Resistor [tolerance=±1% resistance=1.5k power=0.25 package=THT]
  R31 = Resistor [tolerance=±5% resistance=10M power=0.25 package=THT]
  C10 = Ceramic Capacitor [capacitance=100nF voltage=50V package="100 mil [THT, multilayer]"]
  R29 = Resistor [tolerance=±1% resistance=1k power=0.25 package=THT]
  R32 = Resistor [tolerance=±20% resistance=10M power=0.25 package=THT]
  TRN3-1211 = TRN3-1211
  C9 = Ceramic Capacitor [capacitance=100nF voltage=50V package="100 mil [THT, multilayer]"]
  R27 = Resistor [tolerance=±1% resistance=1k power=0.25 package=THT]
  LM358-2 = LM358 [package=dip08]
  R30 = Resistor [tolerance=±10% resistance=1.5k power=0.25 package=THT]
  ADS1115-1 = Adafruit ADS1115 16Bit I2C ADC [part_number="Adafruit #1085"]
  J17 = screw terminal, 2 pins
  J16 = screw terminal, 4 pins
  J14 = screw terminal, 2 pins
  J15 = screw terminal, 2 pins
  THD_15-1211N2 = THD 15-1211N [package="DIP24 [THT]"]
  I2C-MUX1 = shrouded pin header, 6 pins [form="♂ (shrouded male)"]

nets:
  N1: Raspberry_Pi_1.GPIO2, MCP23008.SDA, ADS1115-2.SDA, ADS1115-1.SDA, I2C-MUX1.pin2
  N2: Raspberry_Pi_1.GPIO3, MCP23008.SCL, ADS1115-2.SCL, ADS1115-1.SCL, I2C-MUX1.pin1
  GND: Raspberry_Pi_1.GND, U2.Pin_2, U2.Pin_4, U4.Pin_2, MCP23008.A2, MCP23008.A1, MCP23008.A0, MCP23008.VSS, U3.Pin_2, U3.Pin_4, U1.Pin_2, ADS1115-2.AIN3, ADS1115-2.AIN2, ADS1115-2.AIN1, ADS1115-2.GND, INA282.pin2, INA282.pin3, INA282.pin7, C1.0, LM358-1.G$1_V-, R31.Pin_0, C10.0, R29.Pin_0, R32.Pin_1, TRN3-1211.pin1, C9.0, R27.Pin_0, LM358-2.G$1_V-, J16.pin1, J16.pin3, J14.pin1, THD_15-1211N2.pin_3, THD_15-1211N2.pin_16, I2C-MUX1.pin3
  VDD: Raspberry_Pi_1.5V, MCP23008.Reset, MCP23008.VDD, ADS1115-2.VDD, INA282.pin6, C1.1, ADS1115-1.ADDR, ADS1115-1.VDD, I2C-MUX1.pin4
  N3: Shunt.Pin_0, U4.Pin_4, U1.Pin_4, INA282.pin1
  N4: Shunt.Pin_1, INA282.pin8, J14.pin2
  N5: R1.Pin_0, MCP23008.GP1
  N6: R1.Pin_1, U4.Pin_1, U3.Pin_1
  N7: U2.Pin_1, R2.Pin_1, U1.Pin_1
  N8: U2.Pin_3, U4.Pin_3, J15.pin1
  N9: R2.Pin_0, MCP23008.GP0
  N10: U3.Pin_3, U1.Pin_3, J15.pin2
  N11: ADS1115-2.AIN0, INA282.pin5
  N12: LM358-1.G$1_OUT, LM358-1.G$1_-IN, R28.Pin_1
  N13: LM358-1.G$1_+IN, R31.Pin_1, J17.pin2
  N14: LM358-1.G$2_+IN, R32.Pin_0, J17.pin1
  N15: LM358-1.G$2_-IN, LM358-1.G$2_OUT, R30.Pin_1
  N16: LM358-1.G$1_V+, C10.1, TRN3-1211.pin3, C9.1, LM358-2.G$1_V+
  N17: R28.Pin_0, R27.Pin_1, LM358-2.G$1_+IN
  N18: R29.Pin_1, LM358-2.G$2_+IN, R30.Pin_0
  N19: TRN3-1211.pin2, J16.pin4, THD_15-1211N2.pin_22
  N20: LM358-2.G$1_OUT, LM358-2.G$1_-IN, ADS1115-1.AIN0
  N21: LM358-2.G$2_-IN, LM358-2.G$2_OUT, ADS1115-1.AIN1
  N22: J16.pin2, THD_15-1211N2.pin_14

notes:
  TX_ Battery
  Electrodes AB
  Ohmpi
  GND +12V
  A   B
  N
  TX
  M
  OhmPi card 3.15
  https://gitlab.irstea.fr/reversaal/OhmPi
  +12V
  GND
  Inpout
  +5V
  Electrodes MN

custom parts:
  Microchip MCP23008 8-bit I/O expander: Provides 8-bit, general purpose, parallel I/O expansion for I2C bus. Datasheet: http://ww1.microchip.com/downloads/en/devicedoc/21919e.pdf
  Adafruit ADS1115 16Bit I2C ADC: For microcontrollers without an analog-to-digital converter or when you want a higher-precision ADC, the ADS1115 provides 16-bit precision at 860 samples/second over I2C. The chip can be configured as 4 single-ended input channels, or two differential channels. As a nice bonus, it even includes a programmable gain amplifier, up to x16, to help boost up smaller single/differential signals to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
  TRN3-1211: DC/DCconverter traco power
  THD 15-1211N: DC/DC Converters
