# Fritzing sketch card_measure_raspberry_v4.00 (saved by Fritzing 0.9.9b)
circuit board: 13.6124cm x 6.53974cm
breadboards: 1

parts:
  Raspberry_Pi_1 = Raspberry Pi 3 [part_number=RPI-3-V1.2]
  Shunt = Resistor [tolerance=±0.1% resistance=0.2 power=0.25 package=THT]
  R1 = Resistor [tolerance=±5% resistance=1.5k power=0.25 package=THT]
  U2 = Sharp PC817 [package=THT]
  R2 = Resistor [tolerance=±5% resistance=1.5k power=0.25 package=THT]
  U4 = Sharp PC817 [package=THT]
  MCP23008 = Microchip MCP23008 8-bit I/O expander [part_number=MCP23008 package="DIP (Dual Inline) [THT]"]
  U3 = Sharp PC817 [package=THT]
  U1 = Sharp PC817 [part_number=AQY211EH package=THT]
  ADS1115-2 = Adafruit ADS1115 16Bit I2C ADC [part_number="Adafruit #1085"]
  INA282 = ina 282 [chip_label=INA282]
  C1 = Ceramic Capacitor [capacitance=100nF package="100 mil [THT, multilayer]"]
  ADS1115-1 = Adafruit ADS1115 16Bit I2C ADC [part_number="Adafruit #1085"]
  J14 = screw terminal, 2 pins
  J15 = screw terminal, 2 pins
  THD_15-1211N2 = THD 15-1211N [package="DIP24 [THT]"]
  I2C-MUX1 = shrouded pin header, 6 pins [form="♂ (shrouded male)"]
  LED1 = LED - 5mm [color="Red (633nm)" current=0.030 package="5 mm [THT]"]
  LED2 = LED - 5mm [color="Red (633nm)" current=0.030 package="5 mm [THT]"]
  R3 = Resistor [tolerance=±5% power=0.25 resistance=220 package=THT]
  R4 = Resistor [tolerance=±5% power=0.25 resistance=220 package=THT]
  U5 = ina128 [package=dip08]
  J16 = screw terminal, 2 pins

nets:
  N1: Raspberry_Pi_1.GPIO2, MCP23008.SDA, ADS1115-2.SDA, ADS1115-1.SDA, I2C-MUX1.pin2
  N2: Raspberry_Pi_1.GPIO3, MCP23008.SCL, ADS1115-2.SCL, ADS1115-1.SCL, I2C-MUX1.pin1
  GND: Raspberry_Pi_1.GND, U2.Pin_2, U4.Pin_2, MCP23008.A2, MCP23008.A1, MCP23008.A0, MCP23008.VSS, U3.Pin_2, U1.Pin_2, ADS1115-2.AIN3, ADS1115-2.AIN2, ADS1115-2.AIN1, ADS1115-2.GND, INA282.pin2, INA282.pin3, INA282.pin7, C1.0, THD_15-1211N2.pin_3, THD_15-1211N2.pin_16, I2C-MUX1.pin3
  VDD: Raspberry_Pi_1.5V, MCP23008.Reset, MCP23008.VDD, ADS1115-2.VDD, INA282.pin6, C1.1, ADS1115-1.ADDR, ADS1115-1.VDD, I2C-MUX1.pin4
  N3: Shunt.Pin_0, U4.Pin_4, U1.Pin_4, INA282.pin1
  N4: Shunt.Pin_1, INA282.pin8, J14.pin2
  N5: R1.Pin_0, MCP23008.GP1, R3.Pin_1
  N6: R1.Pin_1, U4.Pin_1, U3.Pin_1
  N7: U2.Pin_1, R2.Pin_1, U1.Pin_1
  N8: U2.Pin_4, U3.Pin_4, J14.pin1
  N9: U2.Pin_3, U4.Pin_3, J15.pin1
  N10: R2.Pin_0, MCP23008.GP0, R4.Pin_1
  N11: U3.Pin_3, U1.Pin_3, J15.pin2
  N12: ADS1115-2.AIN0, INA282.pin5
  N13: ADS1115-1.AIN0, U5.Vo
  N14: LED1.anode, R4.Pin_0
  N15: LED2.anode, R3.Pin_0
  N16: U5.V-IN, J16.pin2
  N17: U5.V+IN, J16.pin1

notes:
  TX_ Battery
  Electrodes AB
  Ohmpi
  GND +12V
  A   B
  TX
  OhmPi board 4.00
  https://gitlab.irstea.fr/reversaal/OhmPi
  Inpout
  Electrodes MN
  M   N

custom parts:
  Microchip MCP23008 8-bit I/O expander: Provides 8-bit, general purpose, parallel I/O expansion for I2C bus. Datasheet: http://ww1.microchip.com/downloads/en/devicedoc/21919e.pdf
  Adafruit ADS1115 16Bit I2C ADC: For microcontrollers without an analog-to-digital converter or when you want a higher-precision ADC, the ADS1115 provides 16-bit precision at 860 samples/second over I2C. The chip can be configured as 4 single-ended input channels, or two differential channels. As a nice bonus, it even includes a programmable gain amplifier, up to x16, to help boost up smaller single/differential signals to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
  THD 15-1211N: DC/DC Converters
  ina128: low voltage audio power amplifier
